// Logisim project 54766 basicsGate.circ as structural Verilog: 1 circuit, main circuit main
module main (
  input  in_1,
  input  in_2,
  input  in_3,
  input  in_4,
  input  in_5,
  input  in_6,
  input  in_7,
  input  in_8,
  input  in_9,
  input  in_10,
  input  in_11
);

  wire and_2_out, not_1_out, not_2_out, not_3_out, or_2_out;

  // AND_Gate and_1 has open pins: in1=in_1, in3=in_3, out=open
  // OR_Gate or_1 has open pins: in1=in_4, in3=in_6, out=open
  and and_2 (and_2_out, in_7, in_8);
  not not_1 (not_1_out, in_9);
  or or_2 (or_2_out, in_10, in_11);
  LED led_1 (.in(not_1_out));
  not not_2 (not_2_out, in_2);
  not not_3 (not_3_out, in_5);
  LED led_2 (.in(and_2_out));
  LED led_3 (.in(or_2_out));
  LED led_4 (.in(not_2_out));
  LED led_5 (.in(not_3_out));

  // Notes on the sheet:
  //   NAND GATE
  //   NOR GATE
  //   AND GATE
  //   NOT GATE
  //   NOR GATE
endmodule
