// Logisim project D flip flop.circ as structural Verilog: 1 circuit, main circuit main
module main (
  input  D,
  output Q,
  output Q_prime
);

  wire and_1_out, and_2_out, clock_1_out, not_1_out, or_1_out, or_2_out;

  Clock clock_1 (.out(clock_1_out));
  not not_1 (not_1_out, D);
  and and_1 (and_1_out, not_1_out, clock_1_out);
  and and_2 (and_2_out, D, clock_1_out);
  not not_2 (Q, or_1_out);
  or or_1 (or_1_out, and_1_out, Q_prime);
  or or_2 (or_2_out, Q, and_2_out);
  not not_3 (Q_prime, or_2_out);

  // Notes on the sheet:
  //   D Flip Flop
endmodule
