// Logisim project Ripple Counter.circ as structural Verilog: 1 circuit, main circuit main
module main (
  input  in_1,
  input  in_2,
  input  in_3,
  input  in_4
);

  wire clock_1_out, t_ff_1_q, t_ff_1_qn, t_ff_2_q, t_ff_2_qn, t_ff_3_q, t_ff_3_qn, t_ff_4_q, undriven,
       undriven_2, undriven_3, undriven_4;

  Clock clock_1 (.out(clock_1_out));
  T_Flip_Flop t_ff_1 (.clk(clock_1_out), .T(undriven), .Q(t_ff_1_q), .Qn(t_ff_1_qn), .en(1'b0));  // open: preset, reset
  T_Flip_Flop t_ff_2 (.clk(t_ff_1_q), .T(undriven_2), .Q(t_ff_2_q), .Qn(t_ff_2_qn), .en(1'b0));  // open: preset, reset
  T_Flip_Flop t_ff_3 (.clk(t_ff_2_q), .T(undriven_3), .Q(t_ff_3_q), .Qn(t_ff_3_qn), .en(1'b0));  // open: preset, reset
  T_Flip_Flop t_ff_4 (.clk(t_ff_3_q), .T(undriven_4), .Q(t_ff_4_q), .en(1'b0));  // open: Qn, preset, reset
endmodule
