// Logisim project SR Flip Flop.circ as structural Verilog: 1 circuit, main circuit main
module main (
  input  in_1,
  input  in_2
);

  wire and_1_out, and_2_out, clock_1_out, not_1_out, not_2_out, or_1_out, or_2_out;

  Clock clock_1 (.out(clock_1_out));
  and and_1 (and_1_out, in_1, clock_1_out);
  and and_2 (and_2_out, clock_1_out, in_2);
  or or_1 (or_1_out, and_1_out, not_2_out);
  or or_2 (or_2_out, not_1_out, and_2_out);
  not not_1 (not_1_out, or_1_out);
  not not_2 (not_2_out, or_2_out);
  LED led_1 (.in(not_1_out));
  LED led_2 (.in(not_2_out));

  // Notes on the sheet:
  //   SR Flip Flop
endmodule
