// Logisim project jk flip flop.circ as structural Verilog: 1 circuit, main circuit main
module main (
  input  in_1,
  input  in_2
);

  wire and_1_out, and_2_out, and_3_out, and_4_out, clock_1_out, not_1_out, not_2_out, not_3_out, not_4_out;

  Clock clock_1 (.out(clock_1_out));
  and and_1 (and_1_out, not_4_out, in_1, clock_1_out);
  and and_2 (and_2_out, clock_1_out, in_2, not_3_out);
  not not_1 (not_1_out, and_1_out);
  not not_2 (not_2_out, and_2_out);
  not not_3 (not_3_out, and_3_out);
  and and_3 (and_3_out, not_1_out, not_4_out);
  not not_4 (not_4_out, and_4_out);
  and and_4 (and_4_out, not_3_out, not_2_out);
  LED led_1 (.in(not_3_out));
  LED led_2 (.in(not_4_out));

  // Notes on the sheet:
  //   JK Flip Flop
endmodule
